// Logisim project 0921_class.circ as structural Verilog: 1 circuit, main circuit main
module main (
  input  A,
  input  B,
  input  in_3,
  input  in_4,
  input  in_5,
  input  IN_B,
  output out_7,
  output out_8,
  output out_9,
  output out_10
);

  wire and_1_out, and_2_out, and_3_out, not_1_out, not_2_out;

  not not_1 (not_1_out, A);
  not not_2 (not_2_out, in_3);
  and and_1 (and_1_out, not_1_out, B);
  and and_2 (and_2_out, A, B);
  and and_3 (and_3_out, not_2_out, in_3);
  or or_1 (out_9, 1'b0, in_5);
  or or_2 (out_7, and_1_out, and_2_out);
  or or_3 (out_8, and_3_out, in_4);

  assign out_10 = IN_B;
endmodule
