// Logisim project 1003_class.circ as structural Verilog: 1 circuit, main circuit main
module main (
  input  A,
  input  B,
  input  I_A,
  input  I_B,
  input  IN_A,
  input  IN_C,
  input  in_7,
  input  in_8,
  input  in_9,
  input  in_10,
  input  in_11,
  input  Selector,
  output Q,
  output O_Q,
  output OUT_Q,
  output out_16,
  output out_17
);

  wire and_2_out, and_3_out, and_4_out, and_5_out, and_6_out, and_7_out, and_8_out, and_9_out, and_10_out,
       not_1_out, not_2_out, not_3_out, not_4_out, not_5_out, or_3_out, or_4_out;

  and and_1 (Q, A, B);
  and and_2 (and_2_out, I_A, I_B);
  not not_1 (not_1_out, and_3_out);
  and and_3 (and_3_out, I_A, I_B);
  not not_2 (not_2_out, IN_A);
  not not_3 (not_3_out, IN_C);
  not not_4 (not_4_out, in_8);
  not not_5 (not_5_out, Selector);
  or or_1 (O_Q, and_2_out, not_1_out);
  and and_4 (and_4_out, not_2_out, not_3_out);
  and and_5 (and_5_out, IN_A, IN_C);
  and and_6 (and_6_out, in_7, not_4_out);
  and and_7 (and_7_out, in_8, in_9);
  and and_8 (and_8_out, not_4_out, in_8);
  and and_9 (and_9_out, in_10, not_5_out);
  and and_10 (and_10_out, Selector, in_11);
  or or_2 (OUT_Q, and_4_out, and_5_out);
  or or_3 (or_3_out, and_6_out, and_7_out);
  or or_4 (or_4_out, in_9, and_8_out);
  or or_5 (out_17, and_9_out, and_10_out);
  and and_11 (out_16, or_3_out, or_4_out);

  // Notes on the sheet:
  //   Q = A * B
  //   Q = (A * B) + `(A * B)
endmodule
