// Logisim project 1005_class.circ as structural Verilog: 1 circuit, main circuit main
module main (
  input  A,
  input  B,
  input  C,
  input  I_A,
  input  I_B,
  input  I_C,
  output out_7,
  output out_8
);

  wire and_1_out, and_2_out, and_3_out, and_4_out, and_5_out, not_1_out, not_2_out, not_3_out, not_4_out,
       or_1_out;

  not not_1 (not_1_out, A);
  not not_2 (not_2_out, C);
  not not_3 (not_3_out, I_A);
  not not_4 (not_4_out, I_C);
  and and_1 (and_1_out, not_1_out, B);
  and and_2 (and_2_out, B, not_2_out);
  and and_3 (and_3_out, not_2_out, B);
  and and_4 (and_4_out, not_3_out, I_B);
  and and_5 (and_5_out, I_B, not_4_out);
  or or_1 (or_1_out, and_1_out, and_2_out);
  or or_2 (out_8, and_4_out, and_5_out);
  or or_3 (out_7, or_1_out, and_3_out);
endmodule
