// Logisim project 750_basic_blocks.circ as structural Verilog: 1 circuit, main circuit main
module main (
  input  INPUT_A,
  input  INPUT_B,
  input  A,
  input  B,
  input  NOT_INPUT,
  output AND_OUTPUT,
  output OR_OUTPUT,
  output NOT_OUTPUT
);

  and and_1 (AND_OUTPUT, INPUT_A, INPUT_B);
  or or_1 (OR_OUTPUT, A, B);
  not not_1 (NOT_OUTPUT, NOT_INPUT);

  // Notes on the sheet:
  //   AND Gate
  //   OR Gate
endmodule
