// Logisim project 750_basic_logic.circ as structural Verilog: 1 circuit, main circuit main
module main (
  input  A,
  input  B,
  input  C,
  input  BOOLEAN_VARIABLE_A,
  input  AND_BOOLEAN_VAR_A,
  input  in_6,
  input  in_7,
  input  in_8,
  input  in_9,
  input  VAR_A,
  input  VAR_B,
  output F,
  output E,
  output out_14,
  output out_15,
  output out_16,
  output out_17,
  output out_18
);

  wire and_1_out, and_2_out, and_3_out, and_4_out, and_5_out, and_6_out, and_7_out, and_8_out, and_9_out,
       and_10_out, not_1_out, not_2_out, not_3_out, not_4_out, not_5_out, not_6_out, not_7_out, not_8_out,
       not_9_out, or_3_out, or_4_out, or_5_out, or_6_out, or_7_out;

  not not_1 (not_1_out, VAR_A);
  not not_2 (not_2_out, VAR_B);
  and and_1 (and_1_out, A, B);
  not not_3 (not_3_out, A);
  and and_2 (and_2_out, not_3_out, B);
  and and_3 (and_3_out, A, B);
  and and_4 (and_4_out, A, not_4_out);
  not not_4 (not_4_out, B);
  and and_5 (and_5_out, C, not_4_out);
  and and_6 (and_6_out, A, B);
  and and_7 (and_7_out, B, not_5_out);
  not not_5 (not_5_out, C);
  not not_6 (not_6_out, BOOLEAN_VARIABLE_A);
  not not_7 (not_7_out, AND_BOOLEAN_VAR_A);
  not not_8 (not_8_out, in_8);
  not not_9 (not_9_out, in_9);
  and and_8 (and_8_out, not_1_out, VAR_B);
  and and_9 (and_9_out, VAR_A, not_2_out);
  and and_10 (and_10_out, VAR_A, VAR_B);
  or or_1 (out_14, BOOLEAN_VARIABLE_A, not_6_out);
  and and_11 (out_15, AND_BOOLEAN_VAR_A, not_7_out);
  nand nand_1 (out_16, in_6, in_7);
  or or_2 (out_17, not_8_out, not_9_out);
  and and_12 (F, and_1_out, C);
  or or_3 (or_3_out, and_2_out, and_3_out);
  or or_4 (or_4_out, and_4_out, and_5_out);
  or or_5 (or_5_out, and_6_out, and_7_out);
  or or_6 (or_6_out, and_8_out, and_9_out);
  or or_7 (or_7_out, or_3_out, or_4_out);
  or or_8 (E, or_7_out, or_5_out);
  or or_9 (out_18, or_6_out, and_10_out);
endmodule
