// Logisim project ALU.circ as structural Verilog: 1 circuit, main circuit main
module main (
  input  A,
  input  B,
  input  SELECTOR,
  output Q
);

  wire and_1_out, and_2_out, and_3_out, not_1_out, or_1_out;

  and and_1 (and_1_out, A, B);
  or or_1 (or_1_out, A, B);
  not not_1 (not_1_out, SELECTOR);
  and and_2 (and_2_out, and_1_out, not_1_out);
  and and_3 (and_3_out, SELECTOR, or_1_out);
  or or_2 (Q, and_2_out, and_3_out);
endmodule
