// Logisim project ALU_1012.circ as structural Verilog: 1 circuit, main circuit main
module main (
  input  A1,
  input  A0,
  input  B1,
  input  B0,
  input  [1:0] OPERATIONS,
  output Result1,
  output Result0,
  output C_out
);

  wire and_1_out, and_2_out, and_3_out, and_4_out, and_5_out, and_6_out, and_7_out, and_8_out, or_1_out,
       or_2_out, or_3_out, xor_1_out, xor_2_out, xor_3_out, xor_4_out;

  and and_1 (and_1_out, A0, B0);
  or or_1 (or_1_out, A0, B0);
  xor xor_1 (xor_1_out, A0, B0);
  and and_2 (and_2_out, A0, B0);
  and and_3 (and_3_out, A0, 1'b0);
  and and_4 (and_4_out, B0, 1'b0);
  xor xor_2 (xor_2_out, xor_1_out, 1'b0);
  or or_2 (or_2_out, and_2_out, and_3_out, and_4_out);
  Multiplexer #(.enable("false"), .select(2)) multiplexer_1 (
    .in0(and_1_out), .in1(or_1_out), .in2(xor_2_out), .out(Result0), .sel(OPERATIONS));  // open: in3
  D_Flip_Flop d_ff_1 ();  // open: D, clk, Q, Qn, preset, reset
  and and_5 (and_5_out, A1, B1);
  or or_3 (or_3_out, A1, B1);
  xor xor_3 (xor_3_out, A1, B1);
  and and_6 (and_6_out, A1, B1);
  and and_7 (and_7_out, A1, or_2_out);
  and and_8 (and_8_out, B1, or_2_out);
  xor xor_4 (xor_4_out, xor_3_out, or_2_out);
  or or_4 (C_out, and_6_out, and_7_out, and_8_out);
  Multiplexer #(.enable("false"), .select(2)) multiplexer_2 (
    .in0(and_5_out), .in1(or_3_out), .in2(xor_4_out), .out(Result1), .sel(OPERATIONS));  // open: in3

  // Notes on the sheet:
  //   d = a and b;
  //   d = a + b;
  //   MACHINE CODE
  //   00000
  //   Assembly
  //   OR a, b
  //   AND a, b
  //   ADD a, b, c
  //   High Level Language
  //   int a = 0, b = 1
  //   int d = a or b;
  //   AND
  //   OR
  //   Machine Code
  //   01000
  //   00000
  //   10000
  //   Left most 2 bits indicate Operation, next 3 bits are input A, B, and Carry In for Adder Op
  //   CarryOut
  //   Logical OR operation with a and b as input
  //   Logical AND operation with a and b as input
  //   10 == Adder
  //   ADDER operation with a and b as input. Also, c as carry in
  //   ALU - Operations
  //   00 == Logical AND
  //   01 == Logical OR
  //   CarryIn
  //   Result Saved in Memory
  //   AND
  //   OR
endmodule
