// Logisim project basic_blocks.circ as structural Verilog: 1 circuit, main circuit main
module main (
  input  AND_INPUT_A,
  input  AND_INPUT_B,
  input  in_3,
  input  OR_INPUT_A,
  input  OR_INPUT_B,
  output AND_OUTPUT,
  output out_7,
  output OR_OUTPUT
);

  or or_1 (OR_OUTPUT, OR_INPUT_A, OR_INPUT_B);
  and and_1 (AND_OUTPUT, AND_INPUT_A, AND_INPUT_B);
  not not_1 (out_7, in_3);

  // Notes on the sheet:
  //   AND Gate
  //   OR Gate
  //   NOT Gate
endmodule
