// Logisim project basic_logic.circ as structural Verilog: 1 circuit, main circuit main
module main (
  input  INPUT_A,
  input  INPUT_B,
  input  INPUT_C,
  output OUTPUT_F,
  output OUTPUT_E
);

  wire and_1_out, and_2_out, and_3_out, and_5_out, or_2_out;

  and and_1 (and_1_out, INPUT_A, INPUT_B);
  and and_2 (and_2_out, INPUT_B, INPUT_C);
  and and_3 (and_3_out, INPUT_A, INPUT_B);
  and and_4 (OUTPUT_F, and_1_out, INPUT_C);
  and and_5 (and_5_out, INPUT_A, INPUT_C);
  or or_1 (OUTPUT_E, and_2_out, or_2_out);
  or or_2 (or_2_out, and_5_out, and_3_out);
endmodule
