// Logisim project 0921_class.circ as structural Verilog: 1 circuit, main circuit main
module main (
  input  in_1,
  input  in_2,
  input  B,
  input  I_A,
  input  I_B,
  input  in_6,
  input  in_7,
  input  in_8,
  input  in_9,
  output out_10,
  output out_11,
  output out_12,
  output out_13,
  output out_14,
  output out_15
);

  wire and_2_out, and_3_out, and_4_out, and_5_out, and_6_out, not_1_out, not_2_out, not_3_out, not_4_out,
       not_5_out, not_6_out, not_7_out, or_3_out;

  not not_1 (not_1_out, in_1);
  not not_2 (not_2_out, in_6);
  not not_3 (not_3_out, in_7);
  not not_4 (not_4_out, in_8);
  not not_5 (not_5_out, in_9);
  and and_1 (out_10, not_1_out, in_1);
  or or_1 (out_11, 1'b0, in_2);
  not not_6 (not_6_out, I_B);
  not not_7 (not_7_out, I_A);
  and and_2 (and_2_out, not_2_out, not_3_out);
  and and_3 (and_3_out, not_2_out, in_7);
  and and_4 (and_4_out, in_6, not_3_out);
  or or_2 (out_15, not_4_out, not_5_out);
  and and_5 (and_5_out, I_A, not_6_out);
  and and_6 (and_6_out, not_7_out, I_B);
  or or_3 (or_3_out, and_2_out, and_3_out);
  or or_4 (out_13, and_5_out, and_6_out);
  or or_5 (out_14, or_3_out, and_4_out);

  assign out_12 = B;
endmodule
