// Logisim project 1003_class.circ as structural Verilog: 1 circuit, main circuit main
module main (
  input  A,
  input  B,
  input  I_A,
  input  I_B,
  input  I_C,
  output Q,
  output O_Q
);

  wire and_2_out, and_3_out, and_4_out, not_1_out, not_2_out;

  and and_1 (Q, A, B);
  not not_1 (not_1_out, I_A);
  and and_2 (and_2_out, not_1_out, I_B);
  not not_2 (not_2_out, I_B);
  and and_3 (and_3_out, I_A, I_C);
  and and_4 (and_4_out, not_2_out, and_3_out);
  or or_1 (O_Q, and_2_out, and_4_out);

  // Notes on the sheet:
  //   Q = (`A * B) + (A * `B * C)
endmodule
