// Logisim project 1005_class.circ as structural Verilog: 1 circuit, main circuit main
module main (
  input  A,
  input  B,
  input  Carry_In,
  input  [1:0] OPERATION,
  output out_5,
  output Carry_Out
);

  wire adder_1_out, and_1_out, or_1_out;

  Adder #(.width(1)) adder_1 (.a(A), .b(B), .out(adder_1_out), .cin(Carry_In), .cout(Carry_Out));
  and and_1 (and_1_out, A, B);
  or or_1 (or_1_out, A, B);
  Multiplexer #(.enable("false"), .select(2)) multiplexer_1 (
    .in0(and_1_out), .in1(or_1_out), .in2(adder_1_out), .in3(1'b1), .out(out_5), .sel(OPERATION));

  // Notes on the sheet:
  //   INPUT
  //   OPERATION
  //   Selector equals 0 means AND operation 
  //   Selector equals 1 means OR operation 
  //   Selector equals 2 means ADD operation 
  //   MUX - SELECTS TYPE OF OPERATION
  //   OR 1, 0
  //   AND 0,1
  //   int x = 0; int y = 1; z = x || y;
  //   01010
  //   0001
  //   OUTPUT
endmodule
