// Logisim project 1012_ALU.circ as structural Verilog: 1 circuit, main circuit main
module main (
  input  A0,
  input  A1,
  input  B0,
  input  B1,
  input  Cin,
  input  [1:0] Operation,
  output out_7,
  output out_8,
  output out_9
);

  wire and_1_out, and_2_out, and_3_out, and_4_out, and_5_out, and_6_out, and_7_out, and_8_out, or_1_out,
       or_2_out, or_3_out, undriven, undriven_2, xor_1_out, xor_2_out, xor_3_out, xor_4_out;

  and and_1 (and_1_out, A0, B0);
  or or_1 (or_1_out, A0, B0);
  xor xor_1 (xor_1_out, A0, B0);
  and and_2 (and_2_out, A0, B0);
  and and_3 (and_3_out, Cin, B0);
  and and_4 (and_4_out, A0, Cin);
  xor xor_2 (xor_2_out, xor_1_out, Cin);
  or or_2 (or_2_out, and_2_out, and_3_out, and_4_out);
  Multiplexer #(.enable("false"), .select(2)) multiplexer_1 (
    .in0(and_1_out), .in1(or_1_out), .in2(xor_2_out), .in3(undriven), .out(out_8), .sel(Operation));
  and and_5 (and_5_out, A1, B1);
  or or_3 (or_3_out, A1, B1);
  xor xor_3 (xor_3_out, A1, B1);
  and and_6 (and_6_out, A1, B1);
  and and_7 (and_7_out, or_2_out, B1);
  and and_8 (and_8_out, A1, or_2_out);
  xor xor_4 (xor_4_out, xor_3_out, or_2_out);
  or or_4 (out_7, and_6_out, and_7_out, and_8_out);
  Multiplexer #(.enable("false"), .select(2)) multiplexer_2 (
    .in0(and_5_out), .in1(or_3_out), .in2(xor_4_out), .in3(undriven_2), .out(out_9), .sel(Operation));
  D_Flip_Flop d_ff_1 ();  // open: D, clk, Q, Qn, preset, reset

  // Notes on the sheet:
  //   Machine Code
  //   00100
  //   01010
  //   10011
  //   Assembly
  //   AND 1,0
  //   OR 0,1
  //   ADD 0,1,1
  //   ALU0
  //   00 == Logical AND
  //   01 == Logical OR
  //   10 == Adder
  //   int a = 1, b = 0; 
  //   a && b;
  //   Higher Level Language
  //   Machine code format 00000 first 2 bits indicate the operation, last 3 bits indicate input a, b, and c_in
  //   ALU1
  //   Store Results in Memory
endmodule
