// Logisim project logic_basics.circ as structural Verilog: 1 circuit, main circuit main
module main (
  input  INPUT_A,
  input  INPUT_B,
  input  A,
  input  B,
  input  IN_A,
  input  IN_B,
  input  IN_C,
  input  in_8,
  input  in_9,
  input  in_10,
  input  I_A,
  input  AND_INPUT_A,
  input  in_13,
  input  in_14,
  input  in_15,
  input  in_16,
  input  in_17,
  input  in_18,
  input  in_19,
  input  in_20,
  output OUTPUT_C,
  output C,
  output D,
  output out_24,
  output OUTPUT_OR,
  output OUT_AND,
  output out_27,
  output out_28,
  output out_29,
  output out_30
);

  wire and_1_out, and_2_out, and_6_out, not_1_out, not_2_out, not_3_out, not_4_out, not_5_out, not_6_out,
       not_7_out, not_8_out, not_9_out, or_4_out, undriven, undriven_2, undriven_3, undriven_4;

  not not_1 (not_1_out, INPUT_A);
  not not_2 (not_2_out, I_A);
  not not_3 (not_3_out, AND_INPUT_A);
  not not_4 (not_4_out, in_15);
  not not_5 (not_5_out, in_16);
  not not_6 (not_6_out, in_19);
  not not_7 (not_7_out, in_20);
  and and_1 (and_1_out, not_1_out, INPUT_B);
  and and_2 (and_2_out, INPUT_A, INPUT_B);
  and and_3 (out_24, in_8, in_10);
  or or_1 (OUTPUT_OR, I_A, not_2_out);
  and and_4 (OUT_AND, AND_INPUT_A, not_3_out);
  nand nand_1 (out_27, in_13, in_14);
  or or_2 (out_28, not_4_out, not_5_out);
  nor nor_1 (out_29, in_17, in_18);
  and and_5 (out_30, not_6_out, not_7_out);
  or or_3 (OUTPUT_C, and_1_out, and_2_out);
  and and_6 (and_6_out, undriven, undriven_2);
  // NAND_Gate nand_2 is placed but not wired
  or or_4 (or_4_out, undriven_3, undriven_4);
  // NOR_Gate nor_2 is placed but not wired
  not not_8 (not_8_out, and_6_out);
  not not_9 (not_9_out, or_4_out);

  assign C = B;
  assign D = IN_B;
endmodule
