// Logisim project xor.circ as structural Verilog: 1 circuit, main circuit main
module main (
  input  A,
  input  B,
  input  IN_A,
  input  IN_B,
  input  I_A,
  input  I_B,
  input  in_7,
  input  in_8,
  input  in_9,
  input  in_10,
  output C,
  output out_12,
  output out_13,
  output out_14,
  output out_15
);

  wire and_1_out, and_2_out, and_3_out, and_4_out, not_2_out, not_3_out, not_4_out;

  and AND_GATE (C, A, B);
  // OR_Gate or_1 is placed but not wired
  // NOT_Gate not_1 is placed but not wired
  not not_2 (not_2_out, IN_A);
  not not_3 (not_3_out, in_9);
  not not_4 (not_4_out, in_10);
  xor xor_1 (out_14, in_7, in_8);
  and and_1 (and_1_out, not_3_out, in_10);
  and and_2 (and_2_out, in_9, not_4_out);
  and and_3 (and_3_out, not_2_out, IN_B);
  and and_4 (and_4_out, IN_A, IN_B);
  or or_2 (out_15, and_1_out, and_2_out);
  or or_3 (out_12, and_3_out, and_4_out);

  assign out_13 = I_B;
endmodule
